# Fritzing sketch MotorContollerWiiWiring (saved by Fritzing 0.8.3b)
breadboards: 1

parts:
  Part1 = Arduino Uno (Rev3)
  U1 = Wiichuck Adapter
  Part2 = TB6612FNG Breakout v11  # not connected
  PSU1 = Adjustable Breadboard Power Supply  # not connected
  M1 = DC Motor  # not connected
  M2 = DC Motor  # not connected

nets:
  N1: Part1.A4/SDA, U1.SCL
  N2: Part1.A5/SCL, U1.SDA
  N3: Part1.GND, U1.+
  N4: Part1.3V3, U1.-

notes:
  Check the power pins on your Arduino. That header is a different size on different Arduinos Uno revs.

custom parts:
  Wiichuck Adapter: SCP1000 Barometric Pressure sensor. Can sense air pressure and temperature. SPI interface.
