# Fritzing sketch WiichuckWiring (saved by Fritzing 0.8.3b)
breadboards: 1

parts:
  Part1 = Arduino Uno (Rev3)
  U1 = Wiichuck Adapter

nets:
  N1: Part1.A4/SDA, U1.SCL
  N2: Part1.A5/SCL, U1.SDA
  N3: Part1.GND, U1.+
  N4: Part1.3V3, U1.-

custom parts:
  Wiichuck Adapter: SCP1000 Barometric Pressure sensor. Can sense air pressure and temperature. SPI interface.
